// Logisim project finalCPU.circ as structural Verilog: 9 circuits, main circuit main
module main (
);

  wire alu_1_negative, alu_1_out_13, alu_1_out_14, alu_1_out_15, alu_1_out_16, alu_1_overflow,
       alu_1_signoverflow, alu_1_zero, and_1_out, and_2_out, clock_1_out, controlunit_1_readdr0,
       controlunit_1_readdr1, controlunit_1_readr0, controlunit_1_readr1, controlunit_1_ronerepeat,
       controlunit_1_rzerorepeat, controlunit_1_subtract, controlunit_1_writedr0, controlunit_1_writedr1,
       controlunit_1_writer0, controlunit_1_writer1, d_ff_4_qn, d_ff_5_q, d_ff_6_q, d_ff_7_q, d_ff_8_q,
       d_ff_9_q, d_ff_10_q, d_ff_12_q, d_ff_13_q, d_ff_15_q, DR0_out_8, DR0_out_9, DR0_out_10, DR0_out_11,
       DR1_out_8, DR1_out_9, DR1_out_10, DR1_out_11, muxer_1_out_11, muxer_1_out_12, muxer_1_out_13,
       muxer_1_out_14, muxer_1_out_15, muxer_1_out_16, muxer_1_out_17, muxer_1_out_18, or_1_out, or_2_out,
       or_3_out, or_4_out, or_5_out, or_6_out, or_7_out, or_8_out, R0_out_8, R0_out_9, R0_out_10, R0_out_11,
       R1_out_8, R1_out_9, R1_out_10, R1_out_11, ram_1_out_10, ram_1_out_11, ram_1_out_12, ram_1_out_13;
  wire [3:0] controlunit_1_cuout, d_ff_3_q, DR0_out_12;

  Clock clock_1 (.out(clock_1_out));
  and and_1 (and_1_out, clock_1_out, d_ff_4_qn);
  D_Flip_Flop #(.trigger("falling")) d_ff_1 (
    .D(controlunit_1_cuout[2]), .clk(and_1_out), .Q(d_ff_3_q[2]));  // open: Qn, preset, reset
  D_Flip_Flop #(.trigger("falling")) d_ff_2 (
    .D(controlunit_1_cuout[1]), .clk(and_1_out), .Q(d_ff_3_q[1]));  // open: Qn, preset, reset
  D_Flip_Flop #(.trigger("falling")) d_ff_3 (
    .D(controlunit_1_cuout[0]), .clk(and_1_out), .Q(d_ff_3_q[0]));  // open: Qn, preset, reset
  D_Flip_Flop #(.trigger("falling")) d_ff_4 (.D(and_2_out), .clk(and_1_out), .Qn(d_ff_4_qn));  // open: Q, preset, reset
  and and_2 (and_2_out, ram_1_out_10, ram_1_out_11, ram_1_out_12, ram_1_out_13);
  RAM ram_1 (
    .Mode(1'b1), .in_2(and_1_out), .in_3(d_ff_3_q[2]), .in_4(d_ff_3_q[1]), .in_5(d_ff_3_q[0]),
    .out_10(ram_1_out_10), .out_11(ram_1_out_11), .out_12(ram_1_out_12), .out_13(ram_1_out_13));  // open: in_6, in_7, in_8, in_9
  D_Flip_Flop d_ff_5 (.D(ram_1_out_10), .clk(and_1_out), .Q(d_ff_5_q));  // open: Qn, preset, reset
  D_Flip_Flop d_ff_6 (.D(ram_1_out_11), .clk(and_1_out), .Q(d_ff_6_q));  // open: Qn, preset, reset
  D_Flip_Flop d_ff_7 (.D(ram_1_out_12), .clk(and_1_out), .Q(d_ff_7_q));  // open: Qn, preset, reset
  D_Flip_Flop d_ff_8 (.D(ram_1_out_13), .clk(and_1_out), .Q(d_ff_8_q));  // open: Qn, preset, reset
  D_Flip_Flop d_ff_9 (.clk(and_1_out), .Q(d_ff_9_q));  // open: D, Qn, preset, reset
  ControlUnit controlunit_1 (
    .Clock(and_1_out), .IR3(d_ff_5_q), .IR2(d_ff_6_q), .IR1(d_ff_7_q), .IR0(d_ff_8_q), .CUIN(d_ff_3_q),
    .CUJUMP(DR0_out_12), .IsValidInstruction(d_ff_9_q), .ReadDR0(controlunit_1_readdr0),
    .ReadDR1(controlunit_1_readdr1), .WriteDR0(controlunit_1_writedr0), .WriteDR1(controlunit_1_writedr1),
    .WriteR0(controlunit_1_writer0), .WriteR1(controlunit_1_writer1), .ReadR0(controlunit_1_readr0),
    .ReadR1(controlunit_1_readr1), .Subtract(controlunit_1_subtract), .RoneRepeat(controlunit_1_ronerepeat),
    .RzeroRepeat(controlunit_1_rzerorepeat), .CUOUT(controlunit_1_cuout));
  Nibble R1 (
    .in_2(or_1_out), .in_3(or_2_out), .in_4(or_3_out), .in_5(or_4_out), .clock(and_1_out),
    .write(controlunit_1_writer1), .in_1(controlunit_1_readr1), .out_8(R1_out_8), .out_9(R1_out_9),
    .out_10(R1_out_10), .out_11(R1_out_11));  // open: out_12
  Nibble R0 (
    .in_2(or_1_out), .in_3(or_2_out), .in_4(or_3_out), .in_5(or_4_out), .clock(and_1_out),
    .write(controlunit_1_writer0), .in_1(controlunit_1_readr0), .out_8(R0_out_8), .out_9(R0_out_9),
    .out_10(R0_out_10), .out_11(R0_out_11));  // open: out_12
  muxer muxer_1 (
    .L0(R1_out_8), .L1(R1_out_9), .L2(R1_out_10), .L3(R1_out_11), .R0(R0_out_8), .R1(R0_out_9),
    .R2(R0_out_10), .R3(R0_out_11), .RepeatR0(controlunit_1_ronerepeat),
    .RepeatR2(controlunit_1_rzerorepeat), .out_11(muxer_1_out_11), .out_12(muxer_1_out_12),
    .out_13(muxer_1_out_13), .out_14(muxer_1_out_14), .out_15(muxer_1_out_15), .out_16(muxer_1_out_16),
    .out_17(muxer_1_out_17), .out_18(muxer_1_out_18));
  ALU alu_1 (
    .RSelection(d_ff_5_q), .Subtraction(controlunit_1_subtract), .in_5(muxer_1_out_15),
    .in_6(muxer_1_out_16), .in_7(muxer_1_out_17), .in_8(muxer_1_out_18), .in_1(muxer_1_out_11),
    .R1(muxer_1_out_12), .in_3(muxer_1_out_13), .in_4(muxer_1_out_14), .Negative(alu_1_negative),
    .Zero(alu_1_zero), .Overflow(alu_1_overflow), .SignOverflow(alu_1_signoverflow), .out_13(alu_1_out_13),
    .out_14(alu_1_out_14), .out_15(alu_1_out_15), .out_16(alu_1_out_16));
  D_Flip_Flop #(.trigger("falling")) d_ff_10 (
    .D(alu_1_out_13), .clk(and_1_out), .Q(d_ff_10_q));  // open: Qn, preset, reset
  D_Flip_Flop #(.trigger("falling")) d_ff_11 (.D(alu_1_negative), .clk(and_1_out));  // open: Q, Qn, preset, reset
  or or_1 (or_1_out, or_5_out, d_ff_10_q);
  D_Flip_Flop #(.trigger("falling")) d_ff_12 (
    .D(alu_1_out_14), .clk(and_1_out), .Q(d_ff_12_q));  // open: Qn, preset, reset
  or or_2 (or_2_out, or_6_out, d_ff_12_q);
  D_Flip_Flop #(.trigger("falling")) d_ff_13 (
    .D(alu_1_out_15), .clk(and_1_out), .Q(d_ff_13_q));  // open: Qn, preset, reset
  D_Flip_Flop #(.trigger("falling")) d_ff_14 (.D(alu_1_zero), .clk(and_1_out));  // open: Q, Qn, preset, reset
  or or_3 (or_3_out, or_7_out, d_ff_13_q);
  D_Flip_Flop #(.trigger("falling")) d_ff_15 (
    .D(alu_1_out_16), .clk(and_1_out), .Q(d_ff_15_q));  // open: Qn, preset, reset
  D_Flip_Flop #(.trigger("falling")) d_ff_16 (.D(alu_1_overflow), .clk(and_1_out));  // open: Q, Qn, preset, reset
  or or_4 (or_4_out, or_8_out, d_ff_15_q);
  D_Flip_Flop #(.trigger("falling")) d_ff_17 (.D(alu_1_signoverflow), .clk(and_1_out));  // open: Q, Qn, preset, reset
  Nibble DR1 (
    .in_2(d_ff_10_q), .in_3(d_ff_12_q), .in_4(d_ff_13_q), .in_5(d_ff_15_q), .clock(and_1_out),
    .write(controlunit_1_writedr1), .in_1(controlunit_1_readdr1), .out_8(DR1_out_8), .out_9(DR1_out_9),
    .out_10(DR1_out_10), .out_11(DR1_out_11));  // open: out_12
  Nibble DR0 (
    .in_2(d_ff_10_q), .in_3(d_ff_12_q), .in_4(d_ff_13_q), .in_5(d_ff_15_q), .clock(and_1_out),
    .write(controlunit_1_writedr0), .in_1(controlunit_1_readdr0), .out_12(DR0_out_12), .out_8(DR0_out_8),
    .out_9(DR0_out_9), .out_10(DR0_out_10), .out_11(DR0_out_11));
  or or_5 (or_5_out, DR1_out_8, DR0_out_8);
  or or_6 (or_6_out, DR1_out_9, DR0_out_9);
  or or_7 (or_7_out, DR1_out_10, DR0_out_10);
  or or_8 (or_8_out, DR1_out_11, DR0_out_11);

  // Notes on the sheet:
  //   Clock
  //   Aditi Potnis, McGill ID: 261093155
  //   Leonardo Falvo, McGill ID: 26109421
  //   Steps to run:
  //   PC
  //   load instructions bottom up
  //   and DR1 to load into RAM address 1
  //   Halt
  //   1. Load the instruction RAM by going into the RAM circuit
  //   2. Load the data into the Data RAM. Go into DR0 to load data into RAM address 0
  //   Instruction RAM
  //   Instruction Register
  //   Valid instruction parameter to avoid Jumping repeatedly
  //   Status
  //   Negative
  //   Zero
  //   Overflow
  //   Sign Overflow
  //   Data RAM
endmodule

module FullAdder (
  input  in_1,
  input  in_2,
  input  in_3,
  output out_4,
  output out_5
);

  wire and_1_out, and_2_out, xor_1_out;

  xor xor_1 (xor_1_out, in_1, in_2);
  and and_1 (and_1_out, in_2, in_1);
  xor xor_2 (out_4, xor_1_out, in_3);
  and and_2 (and_2_out, xor_1_out, in_3);
  or or_1 (out_5, and_1_out, and_2_out);
endmodule

// FourBitAdder
module fourbitadder (
  input  in_1,
  input  in_2,
  input  in_3,
  input  in_4,
  input  in_5,
  input  in_6,
  input  in_7,
  input  in_8,
  output out_9,
  output out_10,
  output out_11,
  output out_12,
  output out_13,
  output out_14
);

  wire fulladder_3_out_5, fulladder_4_out_5;

  FullAdder fulladder_1 (.in_3(out_10), .in_1(in_2), .in_2(in_5), .out_4(out_11), .out_5(out_9));
  FullAdder fulladder_2 (.in_3(fulladder_3_out_5), .in_1(in_3), .in_2(in_6), .out_4(out_12), .out_5(out_10));
  FullAdder fulladder_3 (.in_3(fulladder_4_out_5), .in_1(in_4), .in_2(in_7), .out_4(out_13), .out_5(fulladder_3_out_5));
  FullAdder fulladder_4 (.in_1(in_1), .in_2(in_8), .out_4(out_14), .out_5(fulladder_4_out_5));  // open: in_3
endmodule

module RAM (
  input  Mode,
  input  in_2,
  input  in_3,
  input  in_4,
  input  in_5,
  input  in_6,
  input  in_7,
  input  in_8,
  input  in_9,
  output out_10,
  output out_11,
  output out_12,
  output out_13
);

  wire and_1_out, and_2_out, and_3_out, and_4_out, and_5_out, and_6_out, and_7_out, and_8_out, and_9_out,
       and_10_out, and_11_out, and_12_out, and_13_out, and_14_out, and_15_out, and_16_out, and_17_out,
       and_18_out, and_19_out, and_20_out, and_21_out, and_22_out, and_23_out, and_24_out, and_25_out,
       and_26_out, and_27_out, and_28_out, and_29_out, and_30_out, and_31_out, and_32_out, and_33_out,
       and_34_out, and_35_out, and_36_out, and_37_out, and_38_out, and_39_out, and_40_out, and_41_out,
       and_42_out, and_43_out, and_44_out, and_45_out, and_46_out, and_47_out, and_48_out, d_ff_1_q,
       d_ff_2_q, d_ff_3_q, d_ff_4_q, d_ff_5_q, d_ff_6_q, d_ff_7_q, d_ff_8_q, d_ff_9_q, d_ff_10_q, d_ff_11_q,
       d_ff_12_q, d_ff_13_q, d_ff_14_q, d_ff_15_q, d_ff_16_q, d_ff_17_q, d_ff_18_q, d_ff_19_q, d_ff_20_q,
       d_ff_21_q, d_ff_22_q, d_ff_23_q, d_ff_24_q, d_ff_25_q, d_ff_26_q, d_ff_27_q, d_ff_28_q, d_ff_29_q,
       d_ff_30_q, d_ff_31_q, d_ff_32_q, d_ff_33_q, d_ff_34_q, d_ff_35_q, d_ff_36_q, d_ff_37_q, d_ff_38_q,
       d_ff_39_q, not_1_out, not_2_out, not_3_out, not_4_out, not_5_out, not_6_out, not_7_out, not_8_out,
       not_9_out, not_10_out, not_11_out, not_12_out, not_13_out, not_14_out, not_15_out, not_16_out,
       not_17_out, not_18_out, not_19_out, not_20_out, not_21_out, not_22_out, not_23_out, not_24_out,
       not_25_out, not_26_out, not_27_out, not_28_out, not_29_out, not_30_out, not_31_out, not_32_out,
       not_33_out, not_34_out, not_35_out, not_36_out, not_37_out, not_38_out, not_39_out, not_40_out,
       not_41_out, not_42_out, not_43_out, not_44_out, not_45_out, not_46_out, not_47_out, not_48_out,
       not_49_out, not_50_out, not_51_out, not_52_out, not_53_out, not_54_out, not_55_out, not_56_out,
       not_57_out, not_58_out, or_1_out, or_2_out, or_3_out, or_4_out;

  and and_1 (and_1_out, Mode, d_ff_1_q, d_ff_2_q, d_ff_3_q);
  and and_2 (and_2_out, Mode, d_ff_1_q, d_ff_2_q, not_34_out);
  and and_3 (and_3_out, Mode, d_ff_1_q, not_21_out, d_ff_3_q);
  and and_4 (and_4_out, Mode, d_ff_1_q, not_21_out, not_34_out);
  and and_5 (and_5_out, Mode, not_8_out, d_ff_2_q, d_ff_3_q);
  and and_6 (and_6_out, Mode, not_8_out, d_ff_2_q, not_34_out);
  and and_7 (and_7_out, Mode, not_8_out, not_21_out, d_ff_3_q);
  and and_8 (and_8_out, Mode, not_21_out, not_34_out);
  not not_1 (not_1_out, Mode);
  D_Flip_Flop d_ff_1 (.D(in_3), .clk(in_2), .Q(d_ff_1_q));  // open: Qn, preset, reset
  not not_2 (not_2_out, in_2);
  not not_3 (not_3_out, not_36_out);
  not not_4 (not_4_out, not_38_out);
  not not_5 (not_5_out, not_40_out);
  not not_6 (not_6_out, not_42_out);
  not not_7 (not_7_out, not_44_out);
  not not_8 (not_8_out, d_ff_1_q);
  D_Flip_Flop d_ff_2 (.D(in_4), .clk(in_2), .Q(d_ff_2_q));  // open: Qn, preset, reset
  not not_9 (not_9_out, not_2_out);
  not not_10 (not_10_out, not_9_out);
  not not_11 (not_11_out, not_3_out);
  not not_12 (not_12_out, not_11_out);
  not not_13 (not_13_out, not_4_out);
  not not_14 (not_14_out, not_13_out);
  not not_15 (not_15_out, not_5_out);
  not not_16 (not_16_out, not_15_out);
  not not_17 (not_17_out, not_6_out);
  not not_18 (not_18_out, not_17_out);
  not not_19 (not_19_out, not_7_out);
  not not_20 (not_20_out, not_19_out);
  not not_21 (not_21_out, d_ff_2_q);
  not not_22 (not_22_out, not_10_out);
  not not_23 (not_23_out, not_22_out);
  not not_24 (not_24_out, not_12_out);
  not not_25 (not_25_out, not_24_out);
  not not_26 (not_26_out, not_14_out);
  not not_27 (not_27_out, not_26_out);
  not not_28 (not_28_out, not_16_out);
  not not_29 (not_29_out, not_28_out);
  not not_30 (not_30_out, not_18_out);
  not not_31 (not_31_out, not_30_out);
  not not_32 (not_32_out, not_20_out);
  not not_33 (not_33_out, not_32_out);
  not not_34 (not_34_out, d_ff_3_q);
  D_Flip_Flop d_ff_3 (.D(in_5), .clk(in_2), .Q(d_ff_3_q));  // open: Qn, preset, reset
  not not_35 (not_35_out, not_23_out);
  not not_36 (not_36_out, not_35_out);
  not not_37 (not_37_out, not_25_out);
  not not_38 (not_38_out, not_37_out);
  not not_39 (not_39_out, not_27_out);
  not not_40 (not_40_out, not_39_out);
  not not_41 (not_41_out, not_29_out);
  not not_42 (not_42_out, not_41_out);
  not not_43 (not_43_out, not_31_out);
  not not_44 (not_44_out, not_43_out);
  not not_45 (not_45_out, not_33_out);
  not not_46 (not_46_out, not_45_out);
  not not_47 (not_47_out, and_9_out);
  and and_9 (and_9_out, not_46_out, not_1_out, d_ff_1_q, d_ff_2_q, d_ff_3_q);
  not not_48 (not_48_out, and_10_out);
  and and_10 (and_10_out, not_46_out, not_1_out, d_ff_1_q, d_ff_2_q, not_34_out);
  not not_49 (not_49_out, and_11_out);
  and and_11 (and_11_out, not_46_out, not_1_out, d_ff_1_q, not_21_out, d_ff_3_q);
  not not_50 (not_50_out, and_12_out);
  and and_12 (and_12_out, not_46_out, not_1_out, d_ff_1_q, not_21_out, not_34_out);
  and and_13 (and_13_out, not_46_out, not_1_out, not_8_out, d_ff_2_q, d_ff_3_q);
  not not_51 (not_51_out, and_13_out);
  and and_14 (and_14_out, not_46_out, not_1_out, not_8_out, d_ff_2_q, not_34_out);
  not not_52 (not_52_out, and_14_out);
  and and_15 (and_15_out, not_46_out, not_1_out, not_8_out, not_21_out, d_ff_3_q);
  not not_53 (not_53_out, and_15_out);
  and and_16 (and_16_out, not_46_out, not_1_out, not_8_out, not_21_out, not_34_out);
  not not_54 (not_54_out, and_16_out);
  D_Flip_Flop d_ff_4 (.D(in_6), .clk(in_2), .Q(d_ff_4_q));  // open: Qn, preset, reset
  D_Flip_Flop d_ff_5 (.D(d_ff_4_q), .clk(not_47_out), .Q(d_ff_5_q));  // open: Qn, preset, reset
  D_Flip_Flop d_ff_6 (.D(d_ff_4_q), .clk(not_48_out), .Q(d_ff_6_q));  // open: Qn, preset, reset
  D_Flip_Flop d_ff_7 (.D(d_ff_4_q), .clk(not_49_out), .Q(d_ff_7_q));  // open: Qn, preset, reset
  D_Flip_Flop d_ff_8 (.D(d_ff_4_q), .clk(not_50_out), .Q(d_ff_8_q));  // open: Qn, preset, reset
  D_Flip_Flop d_ff_9 (.D(d_ff_4_q), .clk(not_51_out), .Q(d_ff_9_q));  // open: Qn, preset, reset
  D_Flip_Flop d_ff_10 (.D(d_ff_4_q), .clk(not_52_out), .Q(d_ff_10_q));  // open: Qn, preset, reset
  D_Flip_Flop d_ff_11 (.D(d_ff_4_q), .clk(not_53_out), .Q(d_ff_11_q));  // open: Qn, preset, reset
  D_Flip_Flop d_ff_12 (.D(d_ff_4_q), .clk(not_54_out), .Q(d_ff_12_q));  // open: Qn, preset, reset
  D_Flip_Flop d_ff_13 (.D(in_7), .clk(in_2), .Q(d_ff_13_q));  // open: Qn, preset, reset
  D_Flip_Flop d_ff_14 (.D(d_ff_13_q), .clk(not_47_out), .Q(d_ff_14_q));  // open: Qn, preset, reset
  D_Flip_Flop d_ff_15 (.D(d_ff_13_q), .clk(not_48_out), .Q(d_ff_15_q));  // open: Qn, preset, reset
  D_Flip_Flop d_ff_16 (.D(d_ff_13_q), .clk(not_49_out), .Q(d_ff_16_q));  // open: Qn, preset, reset
  D_Flip_Flop d_ff_17 (.D(d_ff_13_q), .clk(not_50_out), .Q(d_ff_17_q));  // open: Qn, preset, reset
  D_Flip_Flop d_ff_18 (.D(d_ff_13_q), .clk(not_51_out), .Q(d_ff_18_q));  // open: Qn, preset, reset
  D_Flip_Flop d_ff_19 (.D(d_ff_13_q), .clk(not_52_out), .Q(d_ff_19_q));  // open: Qn, preset, reset
  D_Flip_Flop d_ff_20 (.D(d_ff_13_q), .clk(not_53_out), .Q(d_ff_20_q));  // open: Qn, preset, reset
  D_Flip_Flop d_ff_21 (.D(d_ff_13_q), .clk(not_54_out), .Q(d_ff_21_q));  // open: Qn, preset, reset
  D_Flip_Flop d_ff_22 (.D(in_8), .clk(in_2), .Q(d_ff_22_q));  // open: Qn, preset, reset
  D_Flip_Flop d_ff_23 (.D(d_ff_22_q), .clk(not_47_out), .Q(d_ff_23_q));  // open: Qn, preset, reset
  D_Flip_Flop d_ff_24 (.D(d_ff_22_q), .clk(not_48_out), .Q(d_ff_24_q));  // open: Qn, preset, reset
  D_Flip_Flop d_ff_25 (.D(d_ff_22_q), .clk(not_49_out), .Q(d_ff_25_q));  // open: Qn, preset, reset
  D_Flip_Flop d_ff_26 (.D(d_ff_22_q), .clk(not_50_out), .Q(d_ff_26_q));  // open: Qn, preset, reset
  D_Flip_Flop d_ff_27 (.D(d_ff_22_q), .clk(not_51_out), .Q(d_ff_27_q));  // open: Qn, preset, reset
  D_Flip_Flop d_ff_28 (.D(d_ff_22_q), .clk(not_52_out), .Q(d_ff_28_q));  // open: Qn, preset, reset
  D_Flip_Flop d_ff_29 (.D(d_ff_22_q), .clk(not_53_out), .Q(d_ff_29_q));  // open: Qn, preset, reset
  D_Flip_Flop d_ff_30 (.D(d_ff_22_q), .clk(not_54_out), .Q(d_ff_30_q));  // open: Qn, preset, reset
  D_Flip_Flop d_ff_31 (.D(d_ff_39_q), .clk(not_47_out), .Q(d_ff_31_q));  // open: Qn, preset, reset
  D_Flip_Flop d_ff_32 (.D(d_ff_39_q), .clk(not_48_out), .Q(d_ff_32_q));  // open: Qn, preset, reset
  D_Flip_Flop d_ff_33 (.D(d_ff_39_q), .clk(not_49_out), .Q(d_ff_33_q));  // open: Qn, preset, reset
  D_Flip_Flop d_ff_34 (.D(d_ff_39_q), .clk(not_50_out), .Q(d_ff_34_q));  // open: Qn, preset, reset
  D_Flip_Flop d_ff_35 (.D(d_ff_39_q), .clk(not_51_out), .Q(d_ff_35_q));  // open: Qn, preset, reset
  D_Flip_Flop d_ff_36 (.D(d_ff_39_q), .clk(not_52_out), .Q(d_ff_36_q));  // open: Qn, preset, reset
  D_Flip_Flop d_ff_37 (.D(d_ff_39_q), .clk(not_53_out), .Q(d_ff_37_q));  // open: Qn, preset, reset
  D_Flip_Flop d_ff_38 (.D(d_ff_39_q), .clk(not_54_out), .Q(d_ff_38_q));  // open: Qn, preset, reset
  D_Flip_Flop d_ff_39 (.D(in_9), .clk(in_2), .Q(d_ff_39_q));  // open: Qn, preset, reset
  and and_17 (and_17_out, d_ff_5_q, and_1_out);
  and and_18 (and_18_out, d_ff_6_q, and_2_out);
  and and_19 (and_19_out, d_ff_7_q, and_3_out);
  and and_20 (and_20_out, d_ff_8_q, and_4_out);
  and and_21 (and_21_out, d_ff_9_q, and_5_out);
  and and_22 (and_22_out, d_ff_10_q, and_6_out);
  and and_23 (and_23_out, d_ff_11_q, and_7_out);
  and and_24 (and_24_out, d_ff_12_q, and_8_out);
  D_Flip_Flop d_ff_40 (.D(or_4_out), .clk(not_55_out), .Q(out_10));  // open: Qn, preset, reset
  not not_55 (not_55_out, not_46_out);
  and and_25 (and_25_out, d_ff_14_q, and_1_out);
  and and_26 (and_26_out, d_ff_15_q, and_2_out);
  and and_27 (and_27_out, d_ff_16_q, and_3_out);
  and and_28 (and_28_out, d_ff_17_q, and_4_out);
  and and_29 (and_29_out, d_ff_18_q, and_5_out);
  and and_30 (and_30_out, d_ff_19_q, and_6_out);
  and and_31 (and_31_out, d_ff_20_q, and_7_out);
  and and_32 (and_32_out, d_ff_21_q, and_8_out);
  D_Flip_Flop d_ff_41 (.D(or_3_out), .clk(not_56_out), .Q(out_11));  // open: Qn, preset, reset
  not not_56 (not_56_out, not_46_out);
  and and_33 (and_33_out, d_ff_23_q, and_1_out);
  and and_34 (and_34_out, d_ff_31_q, and_1_out);
  and and_35 (and_35_out, d_ff_24_q, and_2_out);
  and and_36 (and_36_out, d_ff_32_q, and_2_out);
  and and_37 (and_37_out, d_ff_25_q, and_3_out);
  and and_38 (and_38_out, d_ff_33_q, and_3_out);
  and and_39 (and_39_out, d_ff_26_q, and_4_out);
  and and_40 (and_40_out, d_ff_34_q, and_4_out);
  and and_41 (and_41_out, d_ff_27_q, and_5_out);
  and and_42 (and_42_out, d_ff_35_q, and_5_out);
  and and_43 (and_43_out, d_ff_28_q, and_6_out);
  and and_44 (and_44_out, d_ff_36_q, and_6_out);
  and and_45 (and_45_out, d_ff_29_q, and_7_out);
  and and_46 (and_46_out, d_ff_37_q, and_7_out);
  and and_47 (and_47_out, d_ff_30_q, and_8_out);
  and and_48 (and_48_out, d_ff_38_q, and_8_out);
  D_Flip_Flop d_ff_42 (.D(or_2_out), .clk(not_57_out), .Q(out_12));  // open: Qn, preset, reset
  not not_57 (not_57_out, not_46_out);
  D_Flip_Flop d_ff_43 (.D(or_1_out), .clk(not_58_out), .Q(out_13));  // open: Qn, preset, reset
  not not_58 (not_58_out, not_46_out);
  or or_1 (or_1_out, and_34_out, and_36_out, and_38_out, and_40_out, and_42_out, and_44_out, and_46_out, and_48_out);
  or or_2 (or_2_out, and_33_out, and_35_out, and_37_out, and_39_out, and_41_out, and_43_out, and_45_out, and_47_out);
  or or_3 (or_3_out, and_25_out, and_26_out, and_27_out, and_28_out, and_29_out, and_30_out, and_31_out, and_32_out);
  or or_4 (or_4_out, and_17_out, and_18_out, and_19_out, and_20_out, and_21_out, and_22_out, and_23_out, and_24_out);

  // Notes on the sheet:
  //   !! Instructions Will Execute Bottom Up !!
  //   Input Bits
  //   Output Bits
endmodule

module ALU (
  input  in_1,
  input  R1,
  input  in_3,
  input  in_4,
  input  in_5,
  input  in_6,
  input  in_7,
  input  in_8,
  input  Subtraction,
  input  RSelection,
  output Negative,
  output Zero,
  output out_13,
  output out_14,
  output out_15,
  output out_16,
  output Overflow,
  output SignOverflow
);

  wire and_1_out, and_2_out, and_3_out, and_4_out, and_5_out, and_6_out, and_7_out, and_8_out, and_9_out,
       and_10_out, and_11_out, and_12_out, and_13_out, and_14_out, and_15_out, and_16_out, and_17_out,
       and_18_out, and_19_out, and_20_out, and_21_out, and_22_out, fourbitadder_1_out_11,
       fourbitadder_1_out_12, fourbitadder_1_out_13, fourbitadder_1_out_14, fourbitadder_2_out_9,
       fourbitadder_2_out_10, fourbitadder_3_out_11, fourbitadder_3_out_12, fourbitadder_3_out_13,
       fourbitadder_3_out_14, not_1_out, not_2_out, not_3_out, not_4_out, not_5_out, not_6_out, not_7_out,
       not_8_out, not_9_out, not_10_out, not_11_out, not_12_out, not_14_out, not_15_out, or_1_out, or_2_out,
       or_4_out, or_5_out, or_6_out, or_7_out, or_8_out, or_9_out, or_10_out;

  not not_1 (not_1_out, RSelection);
  and and_1 (and_1_out, not_1_out, Subtraction);
  and and_2 (and_2_out, Subtraction, RSelection);
  not not_2 (not_2_out, and_2_out);
  and and_3 (and_3_out, not_2_out, in_1);
  not not_3 (not_3_out, in_5);
  not not_4 (not_4_out, in_1);
  not not_5 (not_5_out, in_1);
  and and_4 (and_4_out, and_2_out, not_5_out);
  or or_1 (or_1_out, and_3_out, and_4_out);
  and and_5 (and_5_out, not_3_out, not_4_out);
  not not_6 (not_6_out, Negative);
  and and_6 (and_6_out, in_5, in_1);
  and and_7 (and_7_out, not_2_out, R1);
  or or_2 (or_2_out, and_7_out, and_10_out);
  and and_8 (and_8_out, Negative, and_5_out);
  and and_9 (and_9_out, not_6_out, and_6_out);
  not not_7 (not_7_out, R1);
  and and_10 (and_10_out, and_2_out, not_7_out);
  or or_3 (SignOverflow, and_8_out, and_9_out);
  and and_11 (and_11_out, not_2_out, in_3);
  and and_12 (and_12_out, and_2_out, not_8_out);
  or or_4 (or_4_out, and_11_out, and_12_out);
  fourbitadder fourbitadder_1 (
    .in_8(or_5_out), .in_1(and_2_out), .in_5(or_1_out), .in_6(or_2_out), .in_7(or_4_out),
    .out_11(fourbitadder_1_out_11), .out_12(fourbitadder_1_out_12), .out_13(fourbitadder_1_out_13),
    .out_14(fourbitadder_1_out_14));  // open: in_2, in_3, in_4, out_9, out_10
  not not_8 (not_8_out, in_3);
  and and_13 (and_13_out, not_2_out, in_4);
  not not_9 (not_9_out, in_4);
  and and_14 (and_14_out, and_2_out, not_9_out);
  or or_5 (or_5_out, and_13_out, and_14_out);
  fourbitadder fourbitadder_2 (
    .in_8(fourbitadder_3_out_14), .in_1(fourbitadder_1_out_14), .in_5(fourbitadder_3_out_11),
    .in_2(fourbitadder_1_out_11), .in_6(fourbitadder_3_out_12), .in_3(fourbitadder_1_out_12),
    .in_7(fourbitadder_3_out_13), .in_4(fourbitadder_1_out_13), .out_9(fourbitadder_2_out_9),
    .out_10(fourbitadder_2_out_10), .out_11(Negative), .out_12(out_14), .out_13(out_15), .out_14(out_16));
  xor xor_1 (Overflow, fourbitadder_2_out_9, fourbitadder_2_out_10);
  not not_10 (not_10_out, and_1_out);
  and and_15 (and_15_out, in_5, not_10_out);
  and and_16 (and_16_out, and_1_out, not_11_out);
  or or_6 (or_6_out, and_15_out, and_16_out);
  not not_11 (not_11_out, in_5);
  and and_17 (and_17_out, not_10_out, in_6);
  or or_7 (or_7_out, and_17_out, and_18_out);
  not not_12 (not_12_out, in_6);
  and and_18 (and_18_out, and_1_out, not_12_out);
  or or_8 (or_8_out, Negative, out_14, out_15, out_16);
  not not_13 (Zero, or_8_out);
  not not_14 (not_14_out, in_7);
  and and_19 (and_19_out, not_10_out, in_7);
  or or_9 (or_9_out, and_19_out, and_20_out);
  and and_20 (and_20_out, and_1_out, not_14_out);
  and and_21 (and_21_out, not_10_out, in_8);
  fourbitadder fourbitadder_3 (
    .in_8(or_10_out), .in_1(and_1_out), .in_5(or_6_out), .in_6(or_7_out), .in_7(or_9_out),
    .out_11(fourbitadder_3_out_11), .out_12(fourbitadder_3_out_12), .out_13(fourbitadder_3_out_13),
    .out_14(fourbitadder_3_out_14));  // open: in_2, in_3, in_4, out_9, out_10
  not not_15 (not_15_out, in_8);
  and and_22 (and_22_out, and_1_out, not_15_out);
  or or_10 (or_10_out, and_21_out, and_22_out);

  assign out_13 = Negative;

  // Notes on the sheet:
  //   RSelection
  //   Output Registers
  //   Check for overflow
  //   Check zero value
  //   R0
  //   Indicate negative value
  //   Status Registers
endmodule

module Instructioner (
  input  in_1,
  input  in_2,
  output Load,
  output Save,
  output Add,
  output Sub
);

  wire not_1_out, not_2_out, or_1_out;

  not not_1 (not_1_out, in_1);
  not not_2 (not_2_out, in_2);
  or or_1 (or_1_out, in_1, in_2);
  and and_1 (Save, not_1_out, in_2);
  and and_2 (Add, in_1, not_2_out);
  and and_3 (Sub, in_1, in_2);
  not not_3 (Load, or_1_out);
endmodule

module Nibble (
  input  in_1,
  input  in_2,
  input  in_3,
  input  in_4,
  input  in_5,
  input  clock,
  input  write,
  output out_8,
  output out_9,
  output out_10,
  output out_11,
  output [3:0] out_12
);

  wire and_1_out;

  and and_1 (and_1_out, clock, write);
  D_Flip_Flop #(.trigger("falling")) d_ff_1 (.D(in_2), .clk(and_1_out), .Q(out_12[3]));  // open: Qn, preset, reset
  D_Flip_Flop #(.trigger("falling")) d_ff_2 (.D(in_3), .clk(and_1_out), .Q(out_12[2]));  // open: Qn, preset, reset
  D_Flip_Flop #(.trigger("falling")) d_ff_3 (.D(in_4), .clk(and_1_out), .Q(out_12[1]));  // open: Qn, preset, reset
  D_Flip_Flop #(.trigger("falling")) d_ff_4 (.D(in_5), .clk(and_1_out), .Q(out_12[0]));  // open: Qn, preset, reset
  and and_2 (out_8, in_1, clock, out_12[3]);
  and and_3 (out_9, in_1, clock, out_12[2]);
  and and_4 (out_10, in_1, clock, out_12[1]);
  and and_5 (out_11, in_1, clock, out_12[0]);

  // Notes on the sheet:
  //   input
  //   read
endmodule

module ControlUnit (
  input  Clock,
  input  IR3,
  input  IR2,
  input  IR1,
  input  IR0,
  input  [3:0] CUIN,
  input  [3:0] CUJUMP,
  input  IsValidInstruction,
  output ReadDR0,
  output ReadDR1,
  output WriteDR0,
  output WriteDR1,
  output WriteR0,
  output WriteR1,
  output ReadR0,
  output ReadR1,
  output Subtract,
  output RoneRepeat,
  output RzeroRepeat,
  output [3:0] CUOUT
);

  wire and_1_out, and_2_out, and_3_out, and_4_out, and_5_out, and_8_out, and_9_out, and_10_out, and_11_out,
       and_17_out, and_18_out, and_19_out, and_20_out, and_21_out, and_22_out, and_23_out, and_24_out,
       fourbitadder_1_out_11, fourbitadder_1_out_12, fourbitadder_1_out_13, fourbitadder_1_out_14, not_1_out,
       not_2_out, not_3_out, not_4_out, not_5_out, not_6_out, not_7_out, not_8_out, not_9_out, not_10_out,
       not_11_out, not_12_out, not_13_out, not_14_out, not_15_out, not_16_out, or_1_out, or_2_out, or_3_out;

  not not_1 (not_1_out, IR3);
  not not_2 (not_2_out, IR1);
  not not_3 (not_3_out, IR2);
  not not_4 (not_4_out, IR0);
  and and_1 (and_1_out, not_1_out, not_2_out, not_3_out, not_4_out);
  fourbitadder fourbitadder_1 (
    .in_8(1'b1), .in_1(CUIN[0]), .in_2(CUIN[3]), .in_3(CUIN[2]), .in_4(CUIN[1]),
    .out_11(fourbitadder_1_out_11), .out_12(fourbitadder_1_out_12), .out_13(fourbitadder_1_out_13),
    .out_14(fourbitadder_1_out_14));  // open: in_5, in_6, in_7, out_9, out_10
  and and_2 (and_2_out, and_1_out, IsValidInstruction);
  not not_5 (not_5_out, IR0);
  not not_6 (not_6_out, IR1);
  Multiplexer multiplexer_1 (.in0(fourbitadder_1_out_12), .in1(CUJUMP[2]), .out(CUOUT[2]), .sel(and_2_out));
  Multiplexer multiplexer_2 (.in0(fourbitadder_1_out_14), .in1(CUJUMP[0]), .out(CUOUT[0]), .sel(and_2_out));
  or or_1 (or_1_out, IR3, IR2, IR1, IR0);
  or or_2 (or_2_out, IR3, IR2);
  not not_7 (not_7_out, IR3);
  not not_8 (not_8_out, IR2);
  Multiplexer multiplexer_3 (.in0(fourbitadder_1_out_11), .in1(CUJUMP[3]), .out(CUOUT[3]), .sel(and_2_out));
  Multiplexer multiplexer_4 (.in0(fourbitadder_1_out_13), .in1(CUJUMP[1]), .out(CUOUT[1]), .sel(and_2_out));
  not not_9 (not_9_out, or_1_out);
  not not_10 (not_10_out, or_2_out);
  and and_3 (and_3_out, not_7_out, IR2);
  and and_4 (and_4_out, IR3, not_8_out);
  and and_5 (and_5_out, IR3, IR2);
  and and_6 (RoneRepeat, or_3_out, IR0, IR1);
  and and_7 (RzeroRepeat, or_3_out, not_5_out, not_6_out);
  and and_8 (and_8_out, not_9_out, Clock);
  and and_9 (and_9_out, not_10_out, Clock);
  and and_10 (and_10_out, and_3_out, Clock);
  and and_11 (and_11_out, and_4_out, Clock);
  and and_12 (Subtract, and_5_out, Clock);
  not not_11 (not_11_out, IR0);
  not not_12 (not_12_out, IR1);
  or or_3 (or_3_out, and_11_out, Subtract);
  not not_13 (not_13_out, IR1);
  and and_13 (ReadDR0, and_9_out, not_14_out);
  not not_14 (not_14_out, IR0);
  and and_14 (ReadDR1, and_9_out, IR0);
  and and_15 (WriteDR0, and_10_out, not_11_out);
  and and_16 (WriteDR1, and_10_out, IR0);
  not not_15 (not_15_out, IR1);
  and and_17 (and_17_out, and_10_out, not_12_out);
  and and_18 (and_18_out, and_10_out, IR1);
  not not_16 (not_16_out, IR0);
  and and_19 (and_19_out, and_9_out, not_15_out);
  and and_20 (and_20_out, and_9_out, IR1);
  and and_21 (and_21_out, IR0, or_3_out);
  and and_22 (and_22_out, not_16_out, or_3_out);
  and and_23 (and_23_out, not_13_out, or_3_out);
  and and_24 (and_24_out, IR1, or_3_out);
  or or_4 (WriteR0, and_19_out, and_23_out);
  or or_5 (WriteR1, and_20_out, and_24_out);
  or or_6 (ReadR0, and_22_out, and_17_out, and_23_out);
  or or_7 (ReadR1, and_21_out, and_18_out, and_24_out);

  // Notes on the sheet:
  //   Fetch +1
  //   JUMP
  //   Load
  //   Save
  //   Add
  //   Sub
endmodule

module muxer (
  input  L0,
  input  L1,
  input  L2,
  input  L3,
  input  R0,
  input  R1,
  input  R2,
  input  R3,
  input  RepeatR0,
  input  RepeatR2,
  output out_11,
  output out_12,
  output out_13,
  output out_14,
  output out_15,
  output out_16,
  output out_17,
  output out_18
);

  Multiplexer multiplexer_1 (.in0(L0), .in1(R0), .out(out_11), .sel(RepeatR2));
  Multiplexer multiplexer_2 (.in0(L1), .in1(R1), .out(out_12), .sel(RepeatR2));
  Multiplexer multiplexer_3 (.in0(L2), .in1(R2), .out(out_13), .sel(RepeatR2));
  Multiplexer multiplexer_4 (.in0(L3), .in1(R3), .out(out_14), .sel(RepeatR2));
  Multiplexer multiplexer_5 (.in0(R0), .in1(L0), .out(out_15), .sel(RepeatR0));
  Multiplexer multiplexer_6 (.in0(R1), .in1(L1), .out(out_16), .sel(RepeatR0));
  Multiplexer multiplexer_7 (.in0(R2), .in1(L2), .out(out_17), .sel(RepeatR0));
  Multiplexer multiplexer_8 (.in0(R3), .in1(L3), .out(out_18), .sel(RepeatR0));

  // Notes on the sheet:
  //   Input 1
  //   Input 2
  //   Repeat 1
  //   Repeat 2
endmodule
