// Logisim project finalProject.circ as structural Verilog: 8 circuits, main circuit main
module main (
);

  wire alu_1_negative, alu_1_out_13, alu_1_out_14, alu_1_out_15, alu_1_out_16, alu_1_overflow, alu_1_zero,
       and_1_out, and_2_out, and_3_out, and_4_out, and_5_out, and_6_out, and_7_out, and_8_out, clock_1_out,
       d_ff_1_q, d_ff_2_q, d_ff_3_q, d_ff_4_qn, d_ff_5_q, d_ff_6_q, d_ff_7_qn, d_ff_8_q, d_ff_8_qn,
       d_ff_10_q, d_ff_12_q, d_ff_13_q, d_ff_14_q, d_ff_16_q, d_ff_17_q, d_ff_17_qn, fourbitadder_1_out_12,
       fourbitadder_1_out_13, fourbitadder_1_out_14, instructioner_1_add, instructioner_1_load,
       instructioner_1_sub, not_1_out, or_1_out, or_2_out, or_3_out, R0_out_8, R0_out_9, R0_out_10,
       R0_out_11, R1_out_8, R1_out_9, R1_out_10, R1_out_11, ram_1_out_10, ram_1_out_11, ram_1_out_12,
       ram_1_out_13;

  Clock clock_1 (.out(clock_1_out));
  and and_1 (and_1_out, clock_1_out, d_ff_4_qn);
  D_Flip_Flop #(.trigger("falling")) d_ff_1 (
    .D(fourbitadder_1_out_12), .clk(and_1_out), .Q(d_ff_1_q));  // open: Qn, preset, reset
  D_Flip_Flop #(.trigger("falling")) d_ff_2 (
    .D(fourbitadder_1_out_13), .clk(and_1_out), .Q(d_ff_2_q));  // open: Qn, preset, reset
  D_Flip_Flop #(.trigger("falling")) d_ff_3 (
    .D(fourbitadder_1_out_14), .clk(and_1_out), .Q(d_ff_3_q));  // open: Qn, preset, reset
  D_Flip_Flop #(.trigger("falling")) d_ff_4 (.D(and_2_out), .clk(and_1_out), .Qn(d_ff_4_qn));  // open: Q, preset, reset
  fourbitadder fourbitadder_1 (
    .in_8(d_ff_3_q), .in_1(1'b1), .in_6(d_ff_1_q), .in_7(d_ff_2_q), .out_12(fourbitadder_1_out_12),
    .out_13(fourbitadder_1_out_13), .out_14(fourbitadder_1_out_14));  // open: in_5, in_2, in_3, in_4, out_9, out_10, out_11
  RAM ram_1 (
    .in_3(d_ff_2_q), .in_1(and_1_out), .in_4(d_ff_1_q), .in_5(1'b1), .in_2(d_ff_3_q), .out_10(ram_1_out_10),
    .out_11(ram_1_out_11), .out_12(ram_1_out_12), .out_13(ram_1_out_13));  // open: in_6, in_7, in_8, in_9
  and and_2 (and_2_out, ram_1_out_13, ram_1_out_12, ram_1_out_11, ram_1_out_10);
  D_Flip_Flop #(.trigger("falling")) d_ff_5 (
    .D(ram_1_out_10), .clk(and_1_out), .Q(d_ff_5_q));  // open: Qn, preset, reset
  D_Flip_Flop #(.trigger("falling")) d_ff_6 (
    .D(ram_1_out_11), .clk(and_1_out), .Q(d_ff_6_q));  // open: Qn, preset, reset
  D_Flip_Flop #(.trigger("falling")) d_ff_7 (
    .D(ram_1_out_12), .clk(and_1_out), .Q(and_1_out), .Qn(d_ff_7_qn));  // open: preset, reset
  D_Flip_Flop #(.trigger("falling")) d_ff_8 (
    .D(ram_1_out_13), .clk(and_1_out), .Q(d_ff_8_q), .Qn(d_ff_8_qn));  // open: preset, reset
  Instructioner instructioner_1 (
    .in_1(d_ff_5_q), .in_2(d_ff_6_q), .Load(instructioner_1_load), .Add(instructioner_1_add),
    .Sub(instructioner_1_sub));  // open: Save
  or or_1 (or_1_out, instructioner_1_sub, instructioner_1_add);
  not not_1 (not_1_out, instructioner_1_load);
  and and_3 (and_3_out, or_1_out, d_ff_8_q);
  and and_4 (and_4_out, not_1_out, and_1_out);
  and and_5 (and_5_out, d_ff_7_qn, not_1_out);
  and and_6 (and_6_out, or_1_out, d_ff_8_qn);
  or or_2 (or_2_out, and_3_out, and_4_out);
  or or_3 (or_3_out, and_5_out, and_6_out);
  Nibble R1 (
    .in_2(d_ff_10_q), .in_3(d_ff_12_q), .in_4(d_ff_13_q), .in_5(d_ff_16_q), .clock(and_1_out),
    .write(and_8_out), .in_1(or_2_out), .out_8(R1_out_8), .out_9(R1_out_9), .out_10(R1_out_10),
    .out_11(R1_out_11));
  Nibble R0 (
    .in_2(d_ff_10_q), .in_3(d_ff_12_q), .in_4(d_ff_13_q), .in_5(d_ff_16_q), .clock(and_1_out),
    .write(and_7_out), .in_1(or_3_out), .out_8(R0_out_8), .out_9(R0_out_9), .out_10(R0_out_10),
    .out_11(R0_out_11));
  ALU alu_1 (
    .Subtraction(instructioner_1_sub), .RSelection(d_ff_8_q), .in_5(R0_out_8), .in_6(R0_out_9),
    .in_7(R0_out_10), .in_8(R0_out_11), .in_1(R1_out_8), .R1(R1_out_9), .in_3(R1_out_10), .in_4(R1_out_11),
    .Negative(alu_1_negative), .Zero(alu_1_zero), .Overflow(alu_1_overflow), .out_13(alu_1_out_13),
    .out_14(alu_1_out_14), .out_15(alu_1_out_15), .out_16(alu_1_out_16));
  D_Flip_Flop #(.trigger("falling")) d_ff_9 (.D(alu_1_negative), .clk(and_1_out));  // open: Q, Qn, preset, reset
  D_Flip_Flop #(.trigger("falling")) d_ff_10 (
    .D(alu_1_out_13), .clk(and_1_out), .Q(d_ff_10_q));  // open: Qn, preset, reset
  D_Flip_Flop #(.trigger("falling")) d_ff_11 (.D(alu_1_zero), .clk(and_1_out));  // open: Q, Qn, preset, reset
  D_Flip_Flop #(.trigger("falling")) d_ff_12 (
    .D(alu_1_out_14), .clk(and_1_out), .Q(d_ff_12_q));  // open: Qn, preset, reset
  D_Flip_Flop #(.trigger("falling")) d_ff_13 (
    .D(alu_1_out_15), .clk(and_1_out), .Q(d_ff_13_q));  // open: Qn, preset, reset
  D_Flip_Flop d_ff_14 (.D(or_1_out), .clk(and_1_out), .Q(d_ff_14_q));  // open: Qn, preset, reset
  and and_7 (and_7_out, d_ff_14_q, d_ff_17_qn);
  and and_8 (and_8_out, d_ff_14_q, d_ff_17_q);
  D_Flip_Flop #(.trigger("falling")) d_ff_15 (.D(alu_1_overflow), .clk(and_1_out));  // open: Q, Qn, preset, reset
  D_Flip_Flop #(.trigger("falling")) d_ff_16 (
    .D(alu_1_out_16), .clk(and_1_out), .Q(d_ff_16_q));  // open: Qn, preset, reset
  D_Flip_Flop d_ff_17 (.D(and_1_out), .clk(and_1_out), .Q(d_ff_17_q), .Qn(d_ff_17_qn));  // open: preset, reset
  D_Flip_Flop d_ff_18 ();  // open: D, clk, Q, Qn, preset, reset

  // Notes on the sheet:
  //   PC
  //   Halt
  //   +1 Iterator
  //   Type of Instruction
  //   Instruction Register
  //   Negative
  //   Status
  //   Zero
  //   Rewrite R
  //   Overflow
  //   0/1 Selector
  //   Rewrite D
endmodule

module FullAdder (
  input  in_1,
  input  in_2,
  input  in_3,
  output out_4,
  output out_5
);

  wire and_1_out, and_2_out, xor_1_out;

  xor xor_1 (xor_1_out, in_1, in_2);
  and and_1 (and_1_out, in_2, in_1);
  xor xor_2 (out_4, xor_1_out, in_3);
  and and_2 (and_2_out, xor_1_out, in_3);
  or or_1 (out_5, and_1_out, and_2_out);
endmodule

// FourBitAdder
module fourbitadder (
  input  in_1,
  input  in_2,
  input  in_3,
  input  in_4,
  input  in_5,
  input  in_6,
  input  in_7,
  input  in_8,
  output out_9,
  output out_10,
  output out_11,
  output out_12,
  output out_13,
  output out_14
);

  wire fulladder_3_out_5, fulladder_4_out_5;

  FullAdder fulladder_1 (.in_3(out_10), .in_1(in_2), .in_2(in_5), .out_4(out_11), .out_5(out_9));
  FullAdder fulladder_2 (.in_3(fulladder_3_out_5), .in_1(in_3), .in_2(in_6), .out_4(out_12), .out_5(out_10));
  FullAdder fulladder_3 (.in_3(fulladder_4_out_5), .in_1(in_4), .in_2(in_7), .out_4(out_13), .out_5(fulladder_3_out_5));
  FullAdder fulladder_4 (.in_1(in_1), .in_2(in_8), .out_4(out_14), .out_5(fulladder_4_out_5));  // open: in_3
endmodule

module RAM (
  input  in_1,
  input  in_2,
  input  in_3,
  input  in_4,
  input  in_5,
  input  in_6,
  input  in_7,
  input  in_8,
  input  in_9,
  output out_10,
  output out_11,
  output out_12,
  output out_13
);

  wire and_1_out, and_2_out, and_3_out, and_4_out, and_5_out, and_6_out, and_7_out, and_8_out, and_9_out,
       and_10_out, and_11_out, and_12_out, and_13_out, and_14_out, and_15_out, and_16_out, and_17_out,
       and_18_out, and_19_out, and_20_out, and_21_out, and_22_out, and_23_out, and_24_out, and_25_out,
       and_26_out, and_27_out, and_28_out, and_29_out, and_30_out, and_31_out, and_32_out, and_33_out,
       and_34_out, and_35_out, and_36_out, and_37_out, and_38_out, and_39_out, and_40_out, and_41_out,
       and_42_out, and_43_out, and_44_out, and_45_out, and_46_out, and_47_out, and_48_out, and_49_out,
       and_50_out, and_51_out, and_52_out, and_53_out, and_54_out, and_55_out, and_56_out, and_57_out,
       and_58_out, and_59_out, and_60_out, and_61_out, and_62_out, and_63_out, and_64_out, and_65_out,
       and_66_out, and_67_out, and_68_out, and_69_out, and_70_out, and_71_out, and_72_out, and_73_out,
       and_74_out, and_75_out, and_76_out, and_77_out, and_78_out, and_79_out, and_80_out, d_ff_1_q,
       d_ff_2_q, d_ff_3_q, d_ff_4_q, d_ff_5_q, d_ff_6_q, d_ff_7_q, d_ff_8_q, d_ff_9_q, d_ff_10_q, d_ff_11_q,
       d_ff_12_q, d_ff_13_q, d_ff_14_q, d_ff_15_q, d_ff_16_q, d_ff_17_q, d_ff_18_q, d_ff_19_q, d_ff_20_q,
       d_ff_21_q, d_ff_22_q, d_ff_23_q, d_ff_25_q, d_ff_29_q, d_ff_30_q, d_ff_31_q, d_ff_32_q, d_ff_33_q,
       d_ff_34_q, d_ff_35_q, d_ff_36_q, d_ff_37_q, d_ff_38_q, d_ff_39_q, d_ff_40_q, d_ff_41_q, d_ff_42_q,
       d_ff_43_q, d_ff_44_q, not_1_out, not_2_out, not_3_out, not_4_out, not_5_out, not_6_out, not_7_out,
       not_8_out, not_9_out, not_10_out, not_11_out, not_12_out, not_13_out, or_1_out, or_2_out, or_3_out,
       or_4_out;

  D_Flip_Flop #(.trigger("falling")) d_ff_1 (.D(in_2), .clk(in_1), .Q(d_ff_1_q));  // open: Qn, preset, reset
  D_Flip_Flop #(.trigger("falling")) d_ff_2 (.D(in_3), .clk(in_1), .Q(d_ff_2_q));  // open: Qn, preset, reset
  not not_1 (not_1_out, d_ff_3_q);
  not not_2 (not_2_out, d_ff_2_q);
  not not_3 (not_3_out, d_ff_2_q);
  not not_4 (not_4_out, d_ff_3_q);
  not not_5 (not_5_out, d_ff_1_q);
  not not_6 (not_6_out, d_ff_1_q);
  not not_7 (not_7_out, d_ff_3_q);
  not not_8 (not_8_out, d_ff_1_q);
  not not_9 (not_9_out, d_ff_2_q);
  not not_10 (not_10_out, d_ff_1_q);
  not not_11 (not_11_out, d_ff_2_q);
  not not_12 (not_12_out, d_ff_3_q);
  D_Flip_Flop #(.trigger("falling")) d_ff_3 (.D(in_4), .clk(in_1), .Q(d_ff_3_q));  // open: Qn, preset, reset
  and and_1 (and_1_out, d_ff_1_q, d_ff_2_q, in_1, d_ff_3_q);
  and and_2 (and_2_out, and_1_out, not_13_out);
  and and_3 (and_3_out, d_ff_1_q, d_ff_2_q, in_1, not_1_out);
  and and_4 (and_4_out, and_3_out, not_13_out);
  and and_5 (and_5_out, d_ff_1_q, not_2_out, in_1, d_ff_3_q);
  and and_6 (and_6_out, and_5_out, not_13_out);
  and and_7 (and_7_out, d_ff_1_q, not_3_out, in_1, not_4_out);
  and and_8 (and_8_out, and_7_out, not_13_out);
  and and_9 (and_9_out, not_5_out, d_ff_2_q, in_1, d_ff_3_q);
  and and_10 (and_10_out, and_9_out, not_13_out);
  and and_11 (and_11_out, not_6_out, d_ff_2_q, in_1, not_7_out);
  and and_12 (and_12_out, and_11_out, not_13_out);
  and and_13 (and_13_out, not_8_out, not_9_out, in_1, d_ff_3_q);
  and and_14 (and_14_out, and_13_out, not_13_out);
  and and_15 (and_15_out, not_10_out, not_11_out, in_1, not_12_out);
  and and_16 (and_16_out, and_15_out, not_13_out);
  D_Flip_Flop #(.trigger("falling")) d_ff_4 (.D(in_5), .clk(in_1), .Q(d_ff_4_q));  // open: Qn, preset, reset
  not not_13 (not_13_out, d_ff_4_q);
  and and_17 (and_17_out, and_1_out, not_13_out, d_ff_13_q);
  D_Flip_Flop #(.trigger("high")) d_ff_5 (.D(and_17_out), .clk(and_2_out), .Q(d_ff_5_q));  // open: Qn, preset, reset
  and and_18 (and_18_out, and_3_out, not_13_out, d_ff_13_q);
  D_Flip_Flop #(.trigger("high")) d_ff_6 (.D(and_18_out), .clk(and_4_out), .Q(d_ff_6_q));  // open: Qn, preset, reset
  and and_19 (and_19_out, and_5_out, not_13_out, d_ff_13_q);
  D_Flip_Flop #(.trigger("high")) d_ff_7 (.D(and_19_out), .clk(and_6_out), .Q(d_ff_7_q));  // open: Qn, preset, reset
  and and_20 (and_20_out, and_7_out, not_13_out, d_ff_13_q);
  D_Flip_Flop #(.trigger("high")) d_ff_8 (.D(and_20_out), .clk(and_8_out), .Q(d_ff_8_q));  // open: Qn, preset, reset
  and and_21 (and_21_out, and_9_out, not_13_out, d_ff_13_q);
  D_Flip_Flop #(.trigger("high")) d_ff_9 (.D(and_21_out), .clk(and_10_out), .Q(d_ff_9_q));  // open: Qn, preset, reset
  and and_22 (and_22_out, and_11_out, not_13_out, d_ff_13_q);
  D_Flip_Flop #(.trigger("high")) d_ff_10 (.D(and_22_out), .clk(and_12_out), .Q(d_ff_10_q));  // open: Qn, preset, reset
  and and_23 (and_23_out, and_13_out, not_13_out, d_ff_13_q);
  D_Flip_Flop #(.trigger("high")) d_ff_11 (.D(and_23_out), .clk(and_14_out), .Q(d_ff_11_q));  // open: Qn, preset, reset
  and and_24 (and_24_out, and_15_out, not_13_out, d_ff_13_q);
  D_Flip_Flop #(.trigger("high")) d_ff_12 (.D(and_24_out), .clk(and_16_out), .Q(d_ff_12_q));  // open: Qn, preset, reset
  or or_1 (or_1_out, and_25_out, and_26_out, and_27_out, and_28_out, and_29_out, and_30_out, and_31_out, and_32_out);
  and and_25 (and_25_out, d_ff_5_q, and_1_out, d_ff_4_q);
  and and_26 (and_26_out, d_ff_6_q, and_3_out, d_ff_4_q);
  and and_27 (and_27_out, d_ff_7_q, and_5_out, d_ff_4_q);
  and and_28 (and_28_out, d_ff_8_q, and_7_out, d_ff_4_q);
  and and_29 (and_29_out, d_ff_9_q, and_9_out, d_ff_4_q);
  and and_30 (and_30_out, d_ff_10_q, and_11_out, d_ff_4_q);
  and and_31 (and_31_out, d_ff_11_q, and_13_out, d_ff_4_q);
  and and_32 (and_32_out, d_ff_12_q, and_15_out, d_ff_4_q);
  D_Flip_Flop #(.trigger("falling")) d_ff_13 (.D(in_6), .clk(in_1), .Q(d_ff_13_q));  // open: Qn, preset, reset
  D_Flip_Flop #(.trigger("falling")) d_ff_14 (.D(in_7), .clk(in_1), .Q(d_ff_14_q));  // open: Qn, preset, reset
  and and_33 (and_33_out, and_1_out, not_13_out, d_ff_14_q);
  D_Flip_Flop #(.trigger("high")) d_ff_15 (.D(and_33_out), .clk(and_2_out), .Q(d_ff_15_q));  // open: Qn, preset, reset
  and and_34 (and_34_out, and_3_out, not_13_out, d_ff_14_q);
  D_Flip_Flop #(.trigger("high")) d_ff_16 (.D(and_34_out), .clk(and_4_out), .Q(d_ff_16_q));  // open: Qn, preset, reset
  and and_35 (and_35_out, and_5_out, not_13_out, d_ff_14_q);
  D_Flip_Flop #(.trigger("high")) d_ff_17 (.D(and_35_out), .clk(and_6_out), .Q(d_ff_17_q));  // open: Qn, preset, reset
  and and_36 (and_36_out, and_7_out, not_13_out, d_ff_14_q);
  D_Flip_Flop #(.trigger("high")) d_ff_18 (.D(and_36_out), .clk(and_8_out), .Q(d_ff_18_q));  // open: Qn, preset, reset
  and and_37 (and_37_out, and_9_out, not_13_out, d_ff_14_q);
  D_Flip_Flop #(.trigger("high")) d_ff_19 (.D(and_37_out), .clk(and_10_out), .Q(d_ff_19_q));  // open: Qn, preset, reset
  and and_38 (and_38_out, and_11_out, not_13_out, d_ff_14_q);
  D_Flip_Flop #(.trigger("high")) d_ff_20 (.D(and_38_out), .clk(and_12_out), .Q(d_ff_20_q));  // open: Qn, preset, reset
  and and_39 (and_39_out, and_13_out, not_13_out, d_ff_14_q);
  D_Flip_Flop #(.trigger("high")) d_ff_21 (.D(and_39_out), .clk(and_14_out), .Q(d_ff_21_q));  // open: Qn, preset, reset
  and and_40 (and_40_out, and_15_out, not_13_out, d_ff_14_q);
  D_Flip_Flop #(.trigger("high")) d_ff_22 (.D(and_40_out), .clk(and_16_out), .Q(d_ff_22_q));  // open: Qn, preset, reset
  D_Flip_Flop #(.trigger("falling")) d_ff_23 (.D(in_8), .clk(in_1), .Q(d_ff_23_q));  // open: Qn, preset, reset
  D_Flip_Flop #(.trigger("high")) d_ff_24 (.D(or_1_out), .clk(in_1), .Q(out_10));  // open: Qn, preset, reset
  or or_2 (or_2_out, and_41_out, and_42_out, and_43_out, and_44_out, and_45_out, and_46_out, and_47_out, and_48_out);
  and and_41 (and_41_out, d_ff_15_q, and_1_out, d_ff_4_q);
  and and_42 (and_42_out, d_ff_16_q, and_3_out, d_ff_4_q);
  and and_43 (and_43_out, d_ff_17_q, and_5_out, d_ff_4_q);
  and and_44 (and_44_out, d_ff_18_q, and_7_out, d_ff_4_q);
  and and_45 (and_45_out, d_ff_19_q, and_9_out, d_ff_4_q);
  and and_46 (and_46_out, d_ff_20_q, and_11_out, d_ff_4_q);
  and and_47 (and_47_out, d_ff_21_q, and_13_out, d_ff_4_q);
  and and_48 (and_48_out, d_ff_22_q, and_15_out, d_ff_4_q);
  D_Flip_Flop #(.trigger("falling")) d_ff_25 (.D(in_9), .clk(in_1), .Q(d_ff_25_q));  // open: Qn, preset, reset
  D_Flip_Flop #(.trigger("high")) d_ff_26 (.D(or_2_out), .clk(in_1), .Q(out_11));  // open: Qn, preset, reset
  D_Flip_Flop #(.trigger("high")) d_ff_27 (.D(or_3_out), .clk(in_1), .Q(out_12));  // open: Qn, preset, reset
  and and_49 (and_49_out, and_1_out, not_13_out, d_ff_23_q);
  and and_50 (and_50_out, and_3_out, not_13_out, d_ff_23_q);
  and and_51 (and_51_out, and_5_out, not_13_out, d_ff_23_q);
  and and_52 (and_52_out, and_7_out, not_13_out, d_ff_23_q);
  and and_53 (and_53_out, and_9_out, not_13_out, d_ff_23_q);
  and and_54 (and_54_out, and_11_out, not_13_out, d_ff_23_q);
  and and_55 (and_55_out, and_13_out, not_13_out, d_ff_23_q);
  and and_56 (and_56_out, and_15_out, not_13_out, d_ff_23_q);
  D_Flip_Flop #(.trigger("high")) d_ff_28 (.D(or_4_out), .clk(in_1), .Q(out_13));  // open: Qn, preset, reset
  D_Flip_Flop #(.trigger("high")) d_ff_29 (.D(and_49_out), .clk(and_2_out), .Q(d_ff_29_q));  // open: Qn, preset, reset
  D_Flip_Flop #(.trigger("high")) d_ff_30 (.D(and_50_out), .clk(and_4_out), .Q(d_ff_30_q));  // open: Qn, preset, reset
  D_Flip_Flop #(.trigger("high")) d_ff_31 (.D(and_51_out), .clk(and_6_out), .Q(d_ff_31_q));  // open: Qn, preset, reset
  D_Flip_Flop #(.trigger("high")) d_ff_32 (.D(and_52_out), .clk(and_8_out), .Q(d_ff_32_q));  // open: Qn, preset, reset
  D_Flip_Flop #(.trigger("high")) d_ff_33 (.D(and_53_out), .clk(and_10_out), .Q(d_ff_33_q));  // open: Qn, preset, reset
  D_Flip_Flop #(.trigger("high")) d_ff_34 (.D(and_54_out), .clk(and_12_out), .Q(d_ff_34_q));  // open: Qn, preset, reset
  D_Flip_Flop #(.trigger("high")) d_ff_35 (.D(and_55_out), .clk(and_14_out), .Q(d_ff_35_q));  // open: Qn, preset, reset
  D_Flip_Flop #(.trigger("high")) d_ff_36 (.D(and_56_out), .clk(and_16_out), .Q(d_ff_36_q));  // open: Qn, preset, reset
  or or_3 (or_3_out, and_57_out, and_58_out, and_59_out, and_60_out, and_61_out, and_62_out, and_63_out, and_64_out);
  and and_57 (and_57_out, d_ff_29_q, and_1_out, d_ff_4_q);
  and and_58 (and_58_out, d_ff_30_q, and_3_out, d_ff_4_q);
  and and_59 (and_59_out, d_ff_31_q, and_5_out, d_ff_4_q);
  and and_60 (and_60_out, d_ff_32_q, and_7_out, d_ff_4_q);
  and and_61 (and_61_out, d_ff_33_q, and_9_out, d_ff_4_q);
  and and_62 (and_62_out, d_ff_34_q, and_11_out, d_ff_4_q);
  and and_63 (and_63_out, d_ff_35_q, and_13_out, d_ff_4_q);
  and and_64 (and_64_out, d_ff_36_q, and_15_out, d_ff_4_q);
  and and_65 (and_65_out, and_1_out, not_13_out, d_ff_25_q);
  D_Flip_Flop #(.trigger("high")) d_ff_37 (.D(and_65_out), .clk(and_2_out), .Q(d_ff_37_q));  // open: Qn, preset, reset
  and and_66 (and_66_out, and_3_out, not_13_out, d_ff_25_q);
  D_Flip_Flop #(.trigger("high")) d_ff_38 (.D(and_66_out), .clk(and_4_out), .Q(d_ff_38_q));  // open: Qn, preset, reset
  and and_67 (and_67_out, and_5_out, not_13_out, d_ff_25_q);
  D_Flip_Flop #(.trigger("high")) d_ff_39 (.D(and_67_out), .clk(and_6_out), .Q(d_ff_39_q));  // open: Qn, preset, reset
  and and_68 (and_68_out, and_7_out, not_13_out, d_ff_25_q);
  D_Flip_Flop #(.trigger("high")) d_ff_40 (.D(and_68_out), .clk(and_8_out), .Q(d_ff_40_q));  // open: Qn, preset, reset
  and and_69 (and_69_out, and_9_out, not_13_out, d_ff_25_q);
  D_Flip_Flop #(.trigger("high")) d_ff_41 (.D(and_69_out), .clk(and_10_out), .Q(d_ff_41_q));  // open: Qn, preset, reset
  and and_70 (and_70_out, and_11_out, not_13_out, d_ff_25_q);
  D_Flip_Flop #(.trigger("high")) d_ff_42 (.D(and_70_out), .clk(and_12_out), .Q(d_ff_42_q));  // open: Qn, preset, reset
  and and_71 (and_71_out, and_13_out, not_13_out, d_ff_25_q);
  D_Flip_Flop #(.trigger("high")) d_ff_43 (.D(and_71_out), .clk(and_14_out), .Q(d_ff_43_q));  // open: Qn, preset, reset
  and and_72 (and_72_out, and_15_out, not_13_out, d_ff_25_q);
  D_Flip_Flop #(.trigger("high")) d_ff_44 (.D(and_72_out), .clk(and_16_out), .Q(d_ff_44_q));  // open: Qn, preset, reset
  or or_4 (or_4_out, and_73_out, and_74_out, and_75_out, and_76_out, and_77_out, and_78_out, and_79_out, and_80_out);
  and and_73 (and_73_out, d_ff_37_q, and_1_out, d_ff_4_q);
  and and_74 (and_74_out, d_ff_38_q, and_3_out, d_ff_4_q);
  and and_75 (and_75_out, d_ff_39_q, and_5_out, d_ff_4_q);
  and and_76 (and_76_out, d_ff_40_q, and_7_out, d_ff_4_q);
  and and_77 (and_77_out, d_ff_41_q, and_9_out, d_ff_4_q);
  and and_78 (and_78_out, d_ff_42_q, and_11_out, d_ff_4_q);
  and and_79 (and_79_out, d_ff_43_q, and_13_out, d_ff_4_q);
  and and_80 (and_80_out, d_ff_44_q, and_15_out, d_ff_4_q);

  // Notes on the sheet:
  //   3-bit address input pins
  //   Mode input pin
  //   4-bit data input pins
  //   4-bit data output pins
endmodule

module ALU (
  input  in_1,
  input  R1,
  input  in_3,
  input  in_4,
  input  in_5,
  input  in_6,
  input  in_7,
  input  in_8,
  input  Subtraction,
  input  RSelection,
  output Negative,
  output Zero,
  output out_13,
  output out_14,
  output out_15,
  output out_16,
  output Overflow
);

  wire and_1_out, and_2_out, and_3_out, and_4_out, and_5_out, and_6_out, and_7_out, and_8_out, and_9_out,
       and_10_out, and_11_out, and_12_out, and_13_out, and_14_out, and_15_out, and_16_out, and_17_out,
       and_18_out, fourbitadder_1_out_11, fourbitadder_1_out_12, fourbitadder_1_out_13,
       fourbitadder_1_out_14, fourbitadder_2_out_9, fourbitadder_2_out_10, fourbitadder_3_out_11,
       fourbitadder_3_out_12, fourbitadder_3_out_13, fourbitadder_3_out_14, not_1_out, not_2_out, not_3_out,
       not_4_out, not_5_out, not_6_out, not_7_out, not_8_out, not_9_out, not_11_out, not_12_out, or_1_out,
       or_2_out, or_3_out, or_4_out, or_5_out, or_6_out, or_7_out, or_8_out, or_9_out;

  not not_1 (not_1_out, RSelection);
  and and_1 (and_1_out, not_1_out, Subtraction);
  and and_2 (and_2_out, Subtraction, RSelection);
  not not_2 (not_2_out, and_2_out);
  and and_3 (and_3_out, not_2_out, in_1);
  not not_3 (not_3_out, in_1);
  and and_4 (and_4_out, and_2_out, not_3_out);
  or or_1 (or_1_out, and_3_out, and_4_out);
  and and_5 (and_5_out, not_2_out, R1);
  or or_2 (or_2_out, and_5_out, and_6_out);
  not not_4 (not_4_out, R1);
  and and_6 (and_6_out, and_2_out, not_4_out);
  and and_7 (and_7_out, not_2_out, in_3);
  and and_8 (and_8_out, and_2_out, not_5_out);
  or or_3 (or_3_out, and_7_out, and_8_out);
  fourbitadder fourbitadder_1 (
    .in_8(or_4_out), .in_1(and_2_out), .in_5(or_1_out), .in_6(or_2_out), .in_7(or_3_out),
    .out_11(fourbitadder_1_out_11), .out_12(fourbitadder_1_out_12), .out_13(fourbitadder_1_out_13),
    .out_14(fourbitadder_1_out_14));  // open: in_2, in_3, in_4, out_9, out_10
  not not_5 (not_5_out, in_3);
  and and_9 (and_9_out, not_2_out, in_4);
  not not_6 (not_6_out, in_4);
  and and_10 (and_10_out, and_2_out, not_6_out);
  or or_4 (or_4_out, and_9_out, and_10_out);
  fourbitadder fourbitadder_2 (
    .in_8(fourbitadder_3_out_14), .in_1(fourbitadder_1_out_14), .in_5(fourbitadder_3_out_11),
    .in_2(fourbitadder_1_out_11), .in_6(fourbitadder_3_out_12), .in_3(fourbitadder_1_out_12),
    .in_7(fourbitadder_3_out_13), .in_4(fourbitadder_1_out_13), .out_9(fourbitadder_2_out_9),
    .out_10(fourbitadder_2_out_10), .out_11(Negative), .out_12(out_14), .out_13(out_15), .out_14(out_16));
  xor xor_1 (Overflow, fourbitadder_2_out_9, fourbitadder_2_out_10);
  not not_7 (not_7_out, and_1_out);
  and and_11 (and_11_out, in_5, not_7_out);
  and and_12 (and_12_out, and_1_out, not_8_out);
  or or_5 (or_5_out, and_11_out, and_12_out);
  not not_8 (not_8_out, in_5);
  and and_13 (and_13_out, not_7_out, in_6);
  or or_6 (or_6_out, and_13_out, and_14_out);
  not not_9 (not_9_out, in_6);
  and and_14 (and_14_out, and_1_out, not_9_out);
  or or_7 (or_7_out, Negative, out_14, out_15, out_16);
  not not_10 (Zero, or_7_out);
  not not_11 (not_11_out, in_7);
  and and_15 (and_15_out, not_7_out, in_7);
  or or_8 (or_8_out, and_15_out, and_16_out);
  and and_16 (and_16_out, and_1_out, not_11_out);
  and and_17 (and_17_out, not_7_out, in_8);
  fourbitadder fourbitadder_3 (
    .in_8(or_9_out), .in_1(and_1_out), .in_5(or_5_out), .in_6(or_6_out), .in_7(or_8_out),
    .out_11(fourbitadder_3_out_11), .out_12(fourbitadder_3_out_12), .out_13(fourbitadder_3_out_13),
    .out_14(fourbitadder_3_out_14));  // open: in_2, in_3, in_4, out_9, out_10
  not not_12 (not_12_out, in_8);
  and and_18 (and_18_out, and_1_out, not_12_out);
  or or_9 (or_9_out, and_17_out, and_18_out);

  assign out_13 = Negative;

  // Notes on the sheet:
  //   Output Registers
  //   Check for overflow
  //   Check zero value
  //   R0
  //   Indicate negative value
  //   Status Registers
endmodule

module Instructioner (
  input  in_1,
  input  in_2,
  output Load,
  output Save,
  output Add,
  output Sub
);

  wire not_1_out, not_2_out, or_1_out;

  not not_1 (not_1_out, in_1);
  not not_2 (not_2_out, in_2);
  or or_1 (or_1_out, in_1, in_2);
  and and_1 (Save, not_1_out, in_2);
  and and_2 (Add, in_1, not_2_out);
  and and_3 (Sub, in_1, in_2);
  not not_3 (Load, or_1_out);
endmodule

module Nibble (
  input  in_1,
  input  in_2,
  input  in_3,
  input  in_4,
  input  in_5,
  input  clock,
  input  write,
  output out_8,
  output out_9,
  output out_10,
  output out_11
);

  wire and_1_out, d_ff_1_q, d_ff_2_q, d_ff_3_q, d_ff_4_q;

  and and_1 (and_1_out, clock, write);
  D_Flip_Flop #(.trigger("falling")) d_ff_1 (.D(in_2), .clk(and_1_out), .Q(d_ff_1_q));  // open: Qn, preset, reset
  D_Flip_Flop #(.trigger("falling")) d_ff_2 (.D(in_3), .clk(and_1_out), .Q(d_ff_2_q));  // open: Qn, preset, reset
  D_Flip_Flop #(.trigger("falling")) d_ff_3 (.D(in_4), .clk(and_1_out), .Q(d_ff_3_q));  // open: Qn, preset, reset
  D_Flip_Flop #(.trigger("falling")) d_ff_4 (.D(in_5), .clk(and_1_out), .Q(d_ff_4_q));  // open: Qn, preset, reset
  and and_2 (out_8, in_1, clock, d_ff_1_q);
  and and_3 (out_9, in_1, clock, d_ff_2_q);
  and and_4 (out_10, in_1, clock, d_ff_3_q);
  and and_5 (out_11, in_1, clock, d_ff_4_q);

  // Notes on the sheet:
  //   input
  //   read
endmodule

module ControlUnit (
  input  Clock,
  input  in_2,
  input  IR_Input,
  input  in_4,
  input  in_5,
  output Jump,
  output out_7,
  output out_8,
  output out_9,
  output out_10,
  output out_11
);

  wire alu_1_out_15, alu_1_out_16, and_1_out, and_3_out, and_4_out, and_5_out, and_6_out, and_7_out,
       and_8_out, and_11_out, and_14_out, and_15_out, and_16_out, and_17_out, and_18_out, and_19_out,
       and_20_out, decoder_1_out0, decoder_1_out1, decoder_1_out2, instructioner_1_add, instructioner_1_load,
       instructioner_1_save, instructioner_1_sub, not_1_out, not_2_out, or_1_out;
  wire [1:0] d_ff_1_q;

  D_Flip_Flop #(.trigger("falling")) d_ff_1 (
    .D(alu_1_out_16), .clk(Clock), .Q(d_ff_1_q[0]));  // open: Qn, preset, reset
  D_Flip_Flop #(.trigger("falling")) d_ff_2 (
    .D(alu_1_out_15), .clk(Clock), .Q(d_ff_1_q[1]));  // open: Qn, preset, reset
  and and_1 (and_1_out, in_5, in_4, in_2, IR_Input);
  Decoder #(.select(2)) decoder_1 (
    .out0(decoder_1_out0), .out1(decoder_1_out1), .out2(decoder_1_out2), .sel(d_ff_1_q));  // open: out3, en
  or or_1 (or_1_out, in_2, IR_Input, in_4, in_5);
  not not_1 (not_1_out, and_1_out);
  // AND_Gate and_2 has open pins: in0=not_1_out, in1=or_1_out, out=open
  Instructioner instructioner_1 (
    .in_1(in_2), .in_2(IR_Input), .Load(instructioner_1_load), .Save(instructioner_1_save),
    .Add(instructioner_1_add), .Sub(instructioner_1_sub));
  not not_2 (not_2_out, or_1_out);
  ALU alu_1 (
    .in_7(d_ff_1_q[1]), .in_8(d_ff_1_q[0]), .in_4(1'b1), .out_15(alu_1_out_15), .out_16(alu_1_out_16));  // open: Subtraction, RSelection, in_5, in_6, in_1, R1, in_3, Negative, Zero, Overflow, out_13, out_14
  and and_3 (and_3_out, not_2_out, Clock);
  and and_4 (and_4_out, instructioner_1_load, Clock);
  and and_5 (and_5_out, instructioner_1_save, Clock);
  and and_6 (and_6_out, instructioner_1_add, Clock);
  and and_7 (and_7_out, instructioner_1_sub, Clock);
  and and_8 (and_8_out, decoder_1_out0, and_4_out);
  // AND_Gate and_9 has open pins: in0=decoder_1_out1, in1=and_4_out, out=open
  and and_10 (out_8, decoder_1_out2, and_4_out);
  and and_11 (and_11_out, decoder_1_out0, and_5_out);
  // AND_Gate and_12 has open pins: in0=decoder_1_out1, in1=and_5_out, out=open
  and and_13 (out_9, decoder_1_out2, and_5_out);
  and and_14 (and_14_out, decoder_1_out0, and_6_out);
  and and_15 (and_15_out, decoder_1_out1, and_6_out);
  and and_16 (and_16_out, decoder_1_out2, and_6_out);
  and and_17 (and_17_out, decoder_1_out0, and_7_out);
  and and_18 (and_18_out, decoder_1_out1, and_7_out);
  and and_19 (and_19_out, decoder_1_out2, and_7_out);
  and and_20 (and_20_out, decoder_1_out0, and_3_out);
  and and_21 (Jump, decoder_1_out1, and_3_out);
  // AND_Gate and_22 has open pins: in0=and_3_out, in1=decoder_1_out2, out=open
  or or_2 (out_7, and_20_out, and_8_out, and_11_out, and_14_out, and_17_out);
  or or_3 (out_10, out_8, and_16_out, and_19_out);
  or or_4 (out_11, and_15_out, and_18_out);

  // Notes on the sheet:
  //   Step Counter
  //   Step
  //   JUMP
  //   Load
  //   Save
  //   Add
  //   Sub
  //   Increment PC
  //   R0 Enable
  //   Read from Data RAM
  //   Write to Data RAM
  //   Write to register
endmodule
